// Logisim project Project3Given.circ as structural Verilog: 10 circuits, main circuit CPU15
module main (
  input  EnableBreakpoint,
  input  [14:0] Breakpoint
);

  wire and_2_out, and_3_out, chipset_1_irq, CLK, clock_1_out, cpu15_1_c, cpu15_1_e, cpu15_1_i, cpu15_1_n,
       cpu15_1_o, cpu15_1_z, KBCLR, KBIRQ, KBRD, MEMCS, nand_1_out, RE, TTYCLR, TTYWE, WE;
  wire [6:0] KBDATA, TTYDATA;
  wire [7:0] cpu15_1_srf;
  wire [14:0] ADDR, chipset_1_ivect, chipset_1_led0, chipset_1_led1, chipset_1_led2, chipset_1_led3,
       chipset_1_led4, chipset_1_led5, chipset_1_led6, chipset_1_led7, chipset_1_led8, chipset_1_led9,
       chipset_1_leda, chipset_1_ledb, chipset_1_ledc, chipset_1_ledd, chipset_1_lede, cpu15_1_ib,
       cpu15_1_pc, cpu15_1_r0, cpu15_1_r1, cpu15_1_r2, cpu15_1_r3, cpu15_1_r4, cpu15_1_r5, cpu15_1_r6,
       cpu15_1_r7, cpu15_1_srp, DATA, xnor_1_out;

  Clock clock_1 (.out(clock_1_out));
  nand nand_1 (nand_1_out, EnableBreakpoint, xnor_1_out[0], xnor_1_out[1], xnor_1_out[2], xnor_1_out[3], xnor_1_out[4], xnor_1_out[5], xnor_1_out[6], xnor_1_out[7], xnor_1_out[8], xnor_1_out[9], xnor_1_out[10], xnor_1_out[11], xnor_1_out[12], xnor_1_out[13], xnor_1_out[14], 1'b1);
  and and_1 (CLK, clock_1_out, nand_1_out);
  assign xnor_1_out = ~(Breakpoint ^ cpu15_1_pc);  // XNOR_Gate xnor_1, 15 bits wide
  LED I (.in(cpu15_1_i));
  LED Z (.in(cpu15_1_z));
  LED N (.in(cpu15_1_n));
  LED O (.in(cpu15_1_o));
  LED C (.in(cpu15_1_c));
  LED E (.in(cpu15_1_e));
  and and_2 (and_2_out, WE, MEMCS);
  and and_3 (and_3_out, MEMCS, RE);
  RAM #(.addrWidth(15), .asyncread("true"), .dataWidth(15), .databus("bidir")) ram_1 (
    .addr(ADDR), .we(and_2_out), .oe(and_3_out), .clk(CLK), .data(DATA));
  // Probe on cpu15_1_pc
  // Probe on cpu15_1_ib
  // Probe on cpu15_1_srp
  // Probe on cpu15_1_srf
  // Probe on cpu15_1_r0
  // Probe on cpu15_1_r1
  // Probe on cpu15_1_r2
  // Probe on cpu15_1_r3
  // Probe on cpu15_1_r4
  // Probe on cpu15_1_r5
  // Probe on cpu15_1_r6
  // Probe on cpu15_1_r7
  CPU15 cpu15_1 (
    .I(cpu15_1_i), .Z(cpu15_1_z), .N(cpu15_1_n), .O(cpu15_1_o), .C(cpu15_1_c), .E(cpu15_1_e),
    .PC(cpu15_1_pc), .IB(cpu15_1_ib), .SRP(cpu15_1_srp), .SRF(cpu15_1_srf), .R0(cpu15_1_r0), .R1(cpu15_1_r1),
    .R2(cpu15_1_r2), .R3(cpu15_1_r3), .R4(cpu15_1_r4), .R5(cpu15_1_r5), .R6(cpu15_1_r6), .R7(cpu15_1_r7),
    .CLK(CLK), .IRQ(chipset_1_irq), .RE(RE), .WE(WE), .ADDR(ADDR), .DATAIN(DATA), .DATAOUT(DATA));
  // Probe on ADDR
  // Probe on DATA
  // Probe on chipset_1_ivect
  // Probe on TTYDATA
  CHIPSET chipset_1 (
    .RE(RE), .WE(WE), .ADDR(ADDR), .CPUDATAIN(DATA), .CPUDATAOUT(DATA), .IRQ(chipset_1_irq),
    .IVECT(chipset_1_ivect), .CLK(CLK), .MEMCS(MEMCS), .TTYWR(TTYWE), .TTYCLR(TTYCLR), .TTYDATA(TTYDATA),
    .KBRD(KBRD), .KBCLR(KBCLR), .KBIRQ(KBIRQ), .KBDATA(KBDATA), .LED0(chipset_1_led0), .LED1(chipset_1_led1),
    .LED2(chipset_1_led2), .LED3(chipset_1_led3), .LED4(chipset_1_led4), .LED5(chipset_1_led5),
    .LED6(chipset_1_led6), .LED7(chipset_1_led7), .LED8(chipset_1_led8), .LED9(chipset_1_led9),
    .LEDA(chipset_1_leda), .LEDB(chipset_1_ledb), .LEDC(chipset_1_ledc), .LEDD(chipset_1_ledd),
    .LEDE(chipset_1_lede));
  TTY tty_1 (.data(TTYDATA), .clk(CLK), .we(TTYWE), .clr(TTYCLR));
  Keyboard keyboard_1 (.clk(CLK), .re(KBRD), .clr(KBCLR), .avail(KBIRQ), .data(KBDATA));
  DotMatrix #(.matrixcols(15), .matrixrows(15)) dotmatrix_1 (
    .col0(chipset_1_led0), .col1(chipset_1_led1), .col2(chipset_1_led2), .col3(chipset_1_led3),
    .col4(chipset_1_led4), .col5(chipset_1_led5), .col6(chipset_1_led6), .col7(chipset_1_led7),
    .col8(chipset_1_led8), .col9(chipset_1_led9), .col10(chipset_1_leda), .col11(chipset_1_ledb),
    .col12(chipset_1_ledc), .col13(chipset_1_ledd), .col14(chipset_1_lede));
endmodule

// CPU
module CPU15 (
  input  [14:0] DATAIN,
  input  CLK,
  input  IRQ,
  output [14:0] PC,
  output [14:0] IB,
  output [14:0] SRP,
  output [7:0] SRF,
  output [14:0] R0,
  output [14:0] R1,
  output [14:0] R2,
  output [14:0] R3,
  output [14:0] R4,
  output [14:0] R5,
  output [14:0] R6,
  output [14:0] R7,
  output RE,
  output WE,
  output I,
  output Z,
  output [14:0] ADDR,
  output N,
  output O,
  output C,
  output E,
  output [14:0] DATAOUT
);
endmodule

module CHIPSET (
  input  RE,
  input  WE,
  input  [14:0] ADDR,
  input  [14:0] CPUDATAIN,
  input  KBIRQ,
  input  [6:0] KBDATA,
  input  CLK,
  output MEMCS,
  output TTYWR,
  output [14:0] IVECT,
  output TTYCLR,
  output [6:0] TTYDATA,
  output KBRD,
  output KBCLR,
  output [14:0] CPUDATAOUT,
  output IRQ,
  output [14:0] LED0,
  output [14:0] LED1,
  output [14:0] LED2,
  output [14:0] LED3,
  output [14:0] LED4,
  output [14:0] LED5,
  output [14:0] LED6,
  output [14:0] LED7,
  output [14:0] LED8,
  output [14:0] LED9,
  output [14:0] LEDA,
  output [14:0] LEDB,
  output [14:0] LEDC,
  output [14:0] LEDD,
  output [14:0] LEDE
);

  wire and_1_out, and_8_out, and_10_out, DATA7, IOCS, IVECTADDR, IVECTEN, IVECTRE, KBCS, LED0EN, LED0END,
       LED1EN, LED1END, LED2EN, LED2END, LED3EN, LED3END, LED4EN, LED4END, LED5EN, LED5END, LED6EN, LED6END,
       LED7EN, LED7END, LED8EN, LED8END, LED9EN, LED9END, LEDAEN, LEDAEND, LEDBEN, LEDBEND, LEDCEN, LEDCEND,
       LEDCS, LEDDEN, LEDDEND, LEDEEN, LEDEEND, LEDFEND, LEDRE, multiplexer_17_out, multiplexer_18_out, RWE,
       TTYCS;
  wire [14:0] DATAL0, DATAL1, DATAL2, DATAL3, DATAL4, DATAL5, DATAL6, DATAL7, DATAL8, DATAL9, DATALA, DATALB,
       DATALC, DATALD, DATALE, LEDDATA;
  wire [14:8] KBDATA15;

  assign CPUDATAOUT = KBRD ? {KBDATA15, DATA7, KBDATA} : 15'bz;  // Controlled_Buffer controlled_buffer_1
  assign CPUDATAOUT = LEDRE ? LEDDATA : 15'bz;  // Controlled_Buffer controlled_buffer_2
  assign CPUDATAOUT = IVECTRE ? IVECT : 15'bz;  // Controlled_Buffer controlled_buffer_3
  Register #(.width(15)) register_1 (.D(DATAL0), .en(LED0EN), .Q(LED0), .clk(CLK));  // open: clr
  Register #(.width(15)) register_2 (.D(DATAL1), .en(LED1EN), .Q(LED1), .clk(CLK));  // open: clr
  Register #(.width(15)) register_3 (.D(DATAL2), .en(LED2EN), .Q(LED2), .clk(CLK));  // open: clr
  Register #(.width(15)) register_4 (.D(DATAL3), .en(LED3EN), .Q(LED3), .clk(CLK));  // open: clr
  Register #(.width(15)) register_5 (.D(DATAL4), .en(LED4EN), .Q(LED4), .clk(CLK));  // open: clr
  and and_1 (and_1_out, WE, LEDCS);
  Decoder #(.select(4)) decoder_1 (
    .out0(LED0END), .out1(LED1END), .out2(LED2END), .out3(LED3END), .out4(LED4END), .out5(LED5END),
    .out6(LED6END), .out7(LED7END), .out8(LED8END), .out9(LED9END), .out10(LEDAEND), .out11(LEDBEND),
    .out12(LEDCEND), .out13(LEDDEND), .out14(LEDEEND), .out15(LEDFEND), .sel(ADDR[3:0]), .en(and_1_out));
  Register #(.width(15)) register_6 (.D(DATAL5), .en(LED5EN), .Q(LED5), .clk(CLK));  // open: clr
  Register #(.width(15)) register_7 (.D(DATAL6), .en(LED6EN), .Q(LED6), .clk(CLK));  // open: clr
  Register #(.width(15)) register_8 (.D(DATAL7), .en(LED7EN), .Q(LED7), .clk(CLK));  // open: clr
  Register #(.width(15)) register_9 (.D(DATAL8), .en(LED8EN), .Q(LED8), .clk(CLK));  // open: clr
  Register #(.width(15)) register_10 (.D(DATAL9), .en(LED9EN), .Q(LED9), .clk(CLK));  // open: clr
  or or_1 (LED0EN, LED0END, LEDFEND);
  or or_2 (LED1EN, LED1END, LEDFEND);
  or or_3 (LED2EN, LED2END, LEDFEND);
  or or_4 (LED3EN, LED3END, LEDFEND);
  or or_5 (LED4EN, LED4END, LEDFEND);
  or or_6 (LED5EN, LED5END, LEDFEND);
  or or_7 (LED6EN, LED6END, LEDFEND);
  or or_8 (LED7EN, LED7END, LEDFEND);
  or or_9 (LED8EN, LED8END, LEDFEND);
  or or_10 (LED9EN, LED9END, LEDFEND);
  or or_11 (LEDAEN, LEDAEND, LEDFEND);
  or or_12 (LEDBEN, LEDBEND, LEDFEND);
  or or_13 (LEDCEN, LEDCEND, LEDFEND);
  or or_14 (LEDDEN, LEDDEND, LEDFEND);
  or or_15 (LEDEEN, LEDEEND, LEDFEND);
  Pull_Resistor pull_resistor_1 (.node(KBDATA15[14]));
  Pull_Resistor pull_resistor_2 (.node(KBDATA15[13]));
  Pull_Resistor pull_resistor_3 (.node(KBDATA15[12]));
  Pull_Resistor pull_resistor_4 (.node(KBDATA15[11]));
  Pull_Resistor pull_resistor_5 (.node(KBDATA15[10]));
  Pull_Resistor pull_resistor_6 (.node(KBDATA15[9]));
  Pull_Resistor pull_resistor_7 (.node(KBDATA15[8]));
  Pull_Resistor pull_resistor_8 (.node(DATA7));
  Register #(.width(15)) register_11 (.D(DATALA), .en(LEDAEN), .Q(LEDA), .clk(CLK));  // open: clr
  Register #(.width(15)) register_12 (.D(DATALB), .en(LEDBEN), .Q(LEDB), .clk(CLK));  // open: clr
  Register #(.width(15)) register_13 (.D(DATALC), .en(LEDCEN), .Q(LEDC), .clk(CLK));  // open: clr
  Register #(.width(15)) register_14 (.D(DATALD), .en(LEDDEN), .Q(LEDD), .clk(CLK));  // open: clr
  Register #(.width(15)) register_15 (.D(DATALE), .en(LEDEEN), .Q(LEDE), .clk(CLK));  // open: clr
  Multiplexer #(.width(15)) multiplexer_1 (.in0(CPUDATAIN), .in1(LED1), .out(DATAL0), .sel(LEDFEND));
  Multiplexer #(.width(15)) multiplexer_2 (.in0(CPUDATAIN), .in1(LED2), .out(DATAL1), .sel(LEDFEND));
  Multiplexer #(.width(15)) multiplexer_3 (.in0(CPUDATAIN), .in1(LED3), .out(DATAL2), .sel(LEDFEND));
  Multiplexer #(.width(15)) multiplexer_4 (.in0(CPUDATAIN), .in1(LED4), .out(DATAL3), .sel(LEDFEND));
  Multiplexer #(.width(15)) multiplexer_5 (.in0(CPUDATAIN), .in1(LED5), .out(DATAL4), .sel(LEDFEND));
  Multiplexer #(.select(4), .width(15)) multiplexer_6 (
    .in0(LED0), .in1(LED1), .in2(LED2), .in3(LED3), .in4(LED4), .in5(LED5), .in6(LED6), .in7(LED7),
    .in8(LED8), .in9(LED9), .in10(LEDA), .in11(LEDB), .in12(LEDC), .in13(LEDD), .in14(LEDE),
    .in15({15{1'b0}}), .out(LEDDATA), .sel(ADDR[3:0]));
  Multiplexer #(.width(15)) multiplexer_7 (.in0(CPUDATAIN), .in1(LED6), .out(DATAL5), .sel(LEDFEND));
  Multiplexer #(.width(15)) multiplexer_8 (.in0(CPUDATAIN), .in1(LED7), .out(DATAL6), .sel(LEDFEND));
  Multiplexer #(.width(15)) multiplexer_9 (.in0(CPUDATAIN), .in1(LED8), .out(DATAL7), .sel(LEDFEND));
  Multiplexer #(.width(15)) multiplexer_10 (.in0(CPUDATAIN), .in1(LED9), .out(DATAL8), .sel(LEDFEND));
  Multiplexer #(.width(15)) multiplexer_11 (.in0(CPUDATAIN), .in1(LEDA), .out(DATAL9), .sel(LEDFEND));
  and and_2 (LEDRE, RE, LEDCS);
  Multiplexer #(.width(15)) multiplexer_12 (.in0(CPUDATAIN), .in1(LEDB), .out(DATALA), .sel(LEDFEND));
  Multiplexer #(.width(15)) multiplexer_13 (.in0(CPUDATAIN), .in1(LEDC), .out(DATALB), .sel(LEDFEND));
  Multiplexer #(.width(15)) multiplexer_14 (.in0(CPUDATAIN), .in1(LEDD), .out(DATALC), .sel(LEDFEND));
  Multiplexer #(.width(15)) multiplexer_15 (.in0(CPUDATAIN), .in1(LEDE), .out(DATALD), .sel(LEDFEND));
  Multiplexer #(.width(15)) multiplexer_16 (.in0(CPUDATAIN), .in1(CPUDATAIN), .out(DATALE), .sel(LEDFEND));
  and and_3 (IOCS, ADDR[5], ADDR[6], ADDR[7], ADDR[8], ADDR[9], ADDR[10], ADDR[11], ADDR[12], ADDR[13], ADDR[14], 1'b1);
  and and_4 (TTYCS, IOCS, ADDR[0], ~ADDR[1], ~ADDR[2], ~ADDR[3], ADDR[4]);  // AND_Gate
  and and_5 (KBCS, IOCS, ~ADDR[0], ~ADDR[1], ~ADDR[2], ~ADDR[3], ADDR[4]);  // AND_Gate
  and and_6 (IVECTADDR, ADDR[0], ADDR[1], ADDR[2], ADDR[3], ADDR[4], ADDR[5], ADDR[6], ADDR[7], ADDR[8], ADDR[9], ADDR[10], ADDR[11], ADDR[12], ADDR[13], ADDR[14]);
  and and_7 (TTYWR, TTYCS, WE);
  and and_8 (and_8_out, TTYWR, DATA7);
  and and_9 (KBRD, KBCS, RE);
  and and_10 (and_10_out, KBCS, WE);
  Multiplexer multiplexer_17 (.in0(and_10_out), .in1(1'b0), .out(multiplexer_17_out), .sel(KBCLR));
  and and_11 (LEDCS, IOCS, ~ADDR[4], RWE);  // AND_Gate
  and and_12 (IVECTEN, IVECTADDR, WE);
  and and_13 (IVECTRE, IVECTADDR, RE);
  or or_16 (RWE, RE, WE);
  and and_14 (MEMCS, ~IOCS, RWE);  // AND_Gate
  Multiplexer multiplexer_18 (.in0(and_8_out), .in1(1'b0), .out(multiplexer_18_out), .sel(TTYCLR));
  D_Flip_Flop d_ff_1 (.clk(CLK), .D(multiplexer_17_out), .Q(KBCLR));  // open: Qn, preset, reset
  Register #(.width(15)) register_16 (.D(CPUDATAIN), .en(IVECTEN), .Q(IVECT), .clk(CLK));  // open: clr
  D_Flip_Flop d_ff_2 (.clk(CLK), .D(multiplexer_18_out), .Q(TTYCLR));  // open: Qn, preset, reset

  assign IRQ = KBIRQ;
  assign TTYDATA = CPUDATAIN[6:0];

  // Other names for the same wires on the sheet: DATA[14:0] = CPUDATAIN; KBDATA15[7:0] = {DATA7, KBDATA}
endmodule

module ADDER15 (
  input  [14:0] A,
  input  [14:0] B,
  input  CIN,
  output COUT,
  output [14:0] S
);

  wire cla_1_cout, cla_2_cout;

  CLA cla_1 (.A(A[4:0]), .B(B[4:0]), .CIN(CIN), .COUT(cla_1_cout), .S(S[4:0]));
  CLA cla_2 (.A(A[9:5]), .B(B[9:5]), .CIN(cla_1_cout), .COUT(cla_2_cout), .S(S[9:5]));
  CLA cla_3 (.A(A[14:10]), .B(B[14:10]), .CIN(cla_2_cout), .COUT(COUT), .S(S[14:10]));
endmodule

module REGS15 (
  input  [14:0] D,
  input  W,
  input  [2:0] SelD,
  input  CLK,
  input  [2:0] SelA,
  input  [2:0] SelB,
  output [14:0] R0,
  output [14:0] R1,
  output [14:0] R2,
  output [14:0] R3,
  output [14:0] R4,
  output [14:0] R5,
  output [14:0] R6,
  output [14:0] R7,
  output [14:0] A,
  output [14:0] B
);

  wire R0write, R1write, R2write, R4write, R5write, R6write, R7write;

  Register #(.width(15)) register_1 (.D(D), .en(R0write), .clk(CLK), .Q(R0));  // open: clr
  Register #(.width(15)) register_2 (.D(D), .en(R2write), .clk(CLK), .Q(R2));  // open: clr
  Register #(.width(15)) register_3 (.D(D), .en(R4write), .clk(CLK), .Q(R4));  // open: clr
  Register #(.width(15)) register_4 (.D(D), .en(R6write), .clk(CLK), .Q(R6));  // open: clr
  Register #(.width(15)) register_5 (.D(D), .en(R1write), .clk(CLK), .Q(R1));  // open: clr
  Register #(.width(15)) register_6 (.D(D), .en(R2write), .clk(CLK), .Q(R3));  // open: clr
  Register #(.width(15)) register_7 (.D(D), .en(R5write), .clk(CLK), .Q(R5));  // open: clr
  Register #(.width(15)) register_8 (.D(D), .en(R7write), .clk(CLK), .Q(R7));  // open: clr
  Demultiplexer #(.select(3)) demultiplexer_1 (
    .out0(R0write), .out1(R1write), .out2(R2write), .out3(R2write), .out4(R4write), .out5(R5write),
    .out6(R6write), .out7(R7write), .in(W), .sel(SelD));
  Demultiplexer #(.select(3), .width(15)) demultiplexer_2 (
    .out0(R0), .out1(R0), .out2(R0), .out3(R0), .out4(R0), .out5(R0), .out6(R0), .out7(R0), .in(A), .sel(SelA));
  Demultiplexer #(.select(3), .width(15)) demultiplexer_3 (
    .out0(R0), .out1(R0), .out2(R0), .out3(R0), .out4(R0), .out5(R0), .out6(R0), .out7(R0), .in(B), .sel(SelB));

  // Other names for the same wires on the sheet: R3write = R2write
endmodule

module ALU15 (
  input  [14:0] A,
  input  [14:0] B,
  input  [2:0] OP,
  input  CIN,
  input  OIN,
  output C,
  output O,
  output N,
  output Z,
  output [14:0] R
);
endmodule

module FLAGS8 (
  input  IRQ,
  input  [7:0] NF,
  input  [7:0] WM,
  input  CLK,
  output [7:0] F
);
endmodule

module IMM15 (
  input  [14:0] INST,
  output [14:0] SEXT
);
endmodule

module CLA (
  input  [4:0] A,
  input  [4:0] B,
  input  CIN,
  output COUT,
  output [4:0] S
);

  wire and_1_out, and_2_out, and_3_out, and_4_out, and_5_out, and_6_out, and_7_out, and_8_out, and_9_out,
       and_10_out, and_11_out, and_12_out, and_13_out, C1_out, C2_out, c3_out, c4_out, g0_out, g1_out,
       g2_out, g3_out, g4_out, P0_out, p1_out, p2_out, p3_out, p4_out, pc0_out, pc1_out;

  and g1 (g1_out, B[1], A[1]);
  xor p2 (p2_out, A[2], B[2]);
  and g2 (g2_out, B[2], A[2]);
  xor p3 (p3_out, A[3], B[3]);
  and g3 (g3_out, A[3], B[3]);
  xor p4 (p4_out, A[4], B[4]);
  and g4 (g4_out, A[4], B[4]);
  xor P0 (P0_out, A[0], B[0]);
  and g0 (g0_out, B[0], A[0]);
  xor p1 (p1_out, A[1], B[1]);
  and pc0 (pc0_out, CIN, P0_out);
  and pc1 (pc1_out, C1_out, P0_out, p1_out);
  and and_1 (and_1_out, p1_out, g0_out);
  and and_2 (and_2_out, g1_out, p2_out);
  and and_3 (and_3_out, p2_out, p1_out, g0_out);
  and and_4 (and_4_out, p2_out, p1_out, P0_out, C2_out);
  xor xor_1 (S[0], P0_out, CIN);
  xor xor_2 (S[1], p1_out, C1_out);
  xor xor_3 (S[2], p2_out, C2_out);
  xor xor_4 (S[3], p3_out, c3_out);
  and and_5 (and_5_out, g2_out, p3_out);
  and and_6 (and_6_out, p3_out, p2_out, g1_out);
  and and_7 (and_7_out, p3_out, p2_out, p1_out, g0_out);
  and and_8 (and_8_out, p3_out, p2_out, p1_out, P0_out, c3_out);
  and and_9 (and_9_out, p4_out, g3_out);
  and and_10 (and_10_out, p4_out, p3_out, g2_out);
  and and_11 (and_11_out, p4_out, p3_out, p2_out, g1_out);
  and and_12 (and_12_out, p4_out, p3_out, p2_out, p1_out, g0_out);
  and and_13 (and_13_out, p4_out, p3_out, p2_out, p1_out, P0_out, c4_out);
  or C1 (C1_out, pc0_out, g0_out);
  or C2 (C2_out, pc1_out, g1_out, and_1_out);
  or c3 (c3_out, and_3_out, and_2_out, g2_out, and_4_out);
  or c4 (c4_out, g3_out, and_5_out, and_6_out, and_7_out, and_8_out);
  xor xor_5 (S[4], p4_out, c4_out);
  or c5 (COUT, g4_out, and_9_out, and_10_out, and_11_out, and_12_out, and_13_out);
endmodule

module DECODE15 (
  input  [4:0] OPCODE,
  output SWI,
  output STORE,
  output LOAD,
  output [1:0] ASEL,
  output [1:0] BSEL,
  output [2:0] ALUOP,
  output [2:0] REGDATASRC,
  output REGW,
  output [1:0] FLAGSRC,
  output [7:0] FLAGWM,
  output SRPW,
  output SRFW
);
endmodule
